# Fritzing sketch two_servo_motor (saved by Fritzing 0.9.4)
breadboards: 1

parts:
  パーツ1 = Arduino Uno (Rev3)
  S1 = Pushbutton [package="[THT]"]
  J1 = Basic Servo  # not connected
  YwRobot_Power_Supply1 = YwRobot Breadboard Power Supply [part_number=545043]
  J2 = Basic Servo

nets:
  N1: パーツ1.D9_PWM, J2.pulse
  GND: パーツ1.GND, S1.Pin_1, S1.Pin_2, YwRobot_Power_Supply1.GND#11, J2.gnd
  N2: パーツ1.D2, S1.Pin_3, S1.Pin_4
  N3: YwRobot_Power_Supply1.VCC#9, J2.vcc

custom parts:
  YwRobot Breadboard Power Supply: The YwRobot Breadboard Power Supply (MB-V2) has two power rails; they can be 5V or 3V3. Power to the module can be provided through the female USB socket or through the A10 (female) 2.1mm power jack.
